# Fritzing sketch リニアモーターカー (saved by Fritzing 0.9.5d)
breadboards: 2

parts:
  D1 = LED_BARGRAPH_10 [package=led_bargaph_10]
  S1 = SPST Switch [package=switche-dpdt]
  R1 = Rotary Potentiometer (Small) [maximum_resistance=100kΩ package=THT]
  S2 = SPST Switch [package=switche-dpdt]
  U1 = RELAY [package=OJ]
  パーツ1 = Arduino Nano (Rev3.0) (ICSP)
  U3 = TRANSISTOR_NPN_2 [package=to-92]
  U4 = TRANSISTOR_NPN_2 [package=to-92]
  D2 = Rectifier Diode [part_number=1N4001 package="300 mil [THT]"]
  R2 = Resistor [tolerance=±5% resistance=220 package=THT]
  R3 = Resistor [tolerance=±5% resistance=220 package=THT]
  D3 = Rectifier Diode [part_number=1N4001 package="300 mil [THT]"]
  M1 = DC Motor
  VCC1 = Battery
  GV5-1 = Omron_MY2K_02_12VDC_3A [part_number=GV5-2 package=THT]
  C1 = Ceramic Capacitor [capacitance=100nF package="100 mil [THT, multilayer]"]
  R4 = Resistor [tolerance=±5% resistance=220 package=THT]
  R5 = Resistor [tolerance=±5% resistance=220 package=THT]
  R6 = Resistor [tolerance=±5% resistance=220 package=THT]
  R7 = Resistor [tolerance=±5% resistance=220 package=THT]
  R8 = Resistor [tolerance=±5% resistance=220 package=THT]
  R9 = Resistor [tolerance=±5% resistance=220 package=THT]
  R10 = Resistor [tolerance=±5% resistance=220 package=THT]
  R11 = Resistor [tolerance=±5% resistance=220 package=THT]
  R12 = Resistor [tolerance=±5% resistance=220 package=THT]
  R13 = Resistor [tolerance=±5% resistance=220 package=THT]
  パーツ2 = Arduino Nano (Rev3.0) (ICSP)

nets:
  N1: D1.A_A, パーツ2.D2
  N2: D1.B_A, パーツ2.D3
  N3: D1.C_A, パーツ2.D4
  N4: D1.D_A, パーツ2.D5
  N5: D1.E_A, パーツ2.D6
  N6: D1.F_A, パーツ2.D7
  N7: D1.G_A, パーツ2.D8
  N8: D1.H_A, パーツ2.D9
  N9: D1.I_A, パーツ2.D10
  N10: D1.J_A, パーツ2.D11/MOSI
  N11: D1.J_C, R13.Pin_0
  N12: D1.I_C, R12.Pin_0
  N13: D1.H_C, R10.Pin_0
  N14: D1.G_C, R11.Pin_0
  N15: D1.F_C, R8.Pin_0
  N16: D1.E_C, R9.Pin_0
  N17: D1.D_C, R7.Pin_0
  N18: D1.C_C, R6.Pin_0
  N19: D1.B_C, R5.Pin_0
  N20: D1.A_C, R4.Pin_0
  N21: S1.P, パーツ1.D2
  GND: S1.S, R1.leg1, パーツ1.GND, U3.E, U4.E, R4.Pin_1, R5.Pin_1, R6.Pin_1, R7.Pin_1, R8.Pin_1, R9.Pin_1, R10.Pin_1, R11.Pin_1, R12.Pin_1, R13.Pin_1, パーツ2.GND
  N22: R1.wiper, パーツ1.A0
  5V: R1.leg2, U1.MAIN, U1.NO, パーツ1.5V, U3.C, U4.C, D2.cathode, D2.anode, D3.anode, GV5-1.Set/Reset#89
  N23: S2.O, M1.pin_2, C1.0
  N24: S2.P, GV5-1.Out_2-1, GV5-1.Out_1-2
  N25: U1.COIL2, VCC1.+
  N26: U1.COIL1, GV5-1.Vcc/GND
  N27: パーツ1.D3, R3.Pin_0
  N28: パーツ1.D4, R2.Pin_0
  N29: U3.B, R3.Pin_1
  N30: U4.B, R2.Pin_1
  N31: D3.cathode, GV5-1.Set/Reset#90
  N32: M1.pin_1, GV5-1.Out_1-1, GV5-1.Out_2-2, C1.1
  N33: VCC1.-, GV5-1.GND/Vcc

custom parts:
  Omron_MY2K_02_12VDC_3A: Omron GV5-2, 12VDC @ 2 Amp, Bistable, Low Signal Relay, DPDT, No Coil Polarity
