# Fritzing sketch 距離センサー発展2回路図 (saved by Fritzing 0.9.5d)
circuit board: 8.46667cm x 5.64444cm
breadboards: 1

parts:
  Arduino = Arduino Nano (Rev3.0)
  R1 = Resistor [tolerance=±5% resistance=220 package=THT]
  LED1 = LED - 5mm [color="Red (633nm)" package="5 mm [THT]"]
  距離センサー = Infrared Proximity Sensor

nets:
  GND: Arduino.GND, R1.Pin_0, 距離センサー.GND
  N1: Arduino.D3, LED1.anode
  5V: Arduino.5V, 距離センサー.Vcc
  N2: Arduino.A0, 距離センサー.Vout
  N3: R1.Pin_1, LED1.cathode
