# Fritzing sketch その1 (saved by Fritzing 0.9.5d)
breadboards: 2

parts:
  パーツ1 = Arduino Nano (Rev3.0)
  part = Resistor [tolerance=±5% resistance=220 package=THT]
  part_2 = Resistor [tolerance=±5% resistance=220 package=THT]
  part_3 = Resistor [tolerance=±5% resistance=220 package=THT]
  part_4 = Resistor [tolerance=±5% resistance=220 package=THT]
  part_5 = Resistor [tolerance=±5% resistance=220 package=THT]
  part_6 = Resistor [tolerance=±5% resistance=220 package=THT]
  part_7 = Resistor [tolerance=±5% resistance=220 package=THT]
  part_8 = Resistor [tolerance=±5% resistance=220 package=THT]
  Disp1 = LBT2088AH [part_number=LBT2088AH]

nets:
  GND: パーツ1.GND
  N1: パーツ1.D2, part_8.Pin_1
  N2: パーツ1.D3, part_7.Pin_1
  N3: パーツ1.D4, part_6.Pin_1
  N4: パーツ1.D5, part_5.Pin_1
  N5: パーツ1.D6, part_4.Pin_1
  N6: パーツ1.D7, part_3.Pin_1
  N7: パーツ1.D8, part_2.Pin_1
  N8: パーツ1.D9, part.Pin_1
  N9: パーツ1.D10, Disp1.pin_13
  N10: パーツ1.D11/MOSI, Disp1.pin_3
  N11: パーツ1.D12/MISO, Disp1.pin_4
  5V: パーツ1.5V
  N12: パーツ1.A4, Disp1.pin_16
  N13: パーツ1.A3, Disp1.pin_15
  N14: パーツ1.A2, Disp1.pin_11
  N15: パーツ1.A1, Disp1.pin_6
  N16: パーツ1.A0, Disp1.pin_10
  N17: part.Pin_0, Disp1.pin_5
  N18: part_2.Pin_0, Disp1.pin2
  N19: part_3.Pin_0, Disp1.pin_7
  N20: part_4.Pin_0, Disp1.pin1
  N21: part_5.Pin_0, Disp1.pin_12
  N22: part_6.Pin_0, Disp1.pin_8
  N23: part_7.Pin_0, Disp1.pin_14
  N24: part_8.Pin_0, Disp1.pin_9
