# Fritzing sketch 発展その2 (saved by Fritzing 0.9.5d)
breadboards: 2

parts:
  パーツ1 = Arduino Nano (Rev3.0)
  R1 = Resistor [tolerance=±5% resistance=220 package=THT]
  R2 = Resistor [tolerance=±5% resistance=220 package=THT]
  R3 = Resistor [tolerance=±5% resistance=220 package=THT]
  R4 = Resistor [tolerance=±5% resistance=220 package=THT]
  R5 = Resistor [tolerance=±5% resistance=220 package=THT]
  R6 = Resistor [tolerance=±5% resistance=220 package=THT]
  R7 = Resistor [tolerance=±5% resistance=220 package=THT]
  R8 = Resistor [tolerance=±5% resistance=220 package=THT]
  Disp1 = LBT2088AH [part_number=LBT2088AH]
  KMX52-1 = KMX52-1050 [chip_label=KMX52 package="DIP (Dual Inline) [THT]"]
  R9 = Resistor [tolerance=±5% resistance=220 package=THT]
  S1 = Pushbutton [package="[THT]"]

nets:
  GND: パーツ1.GND, KMX52-1.GND, S1.Pin_2
  N1: パーツ1.D2, R8.Pin_1
  N2: パーツ1.D3, R7.Pin_1
  N3: パーツ1.D4, R6.Pin_1
  N4: パーツ1.D5, R5.Pin_1
  N5: パーツ1.D6, R4.Pin_1
  N6: パーツ1.D7, R3.Pin_1
  N7: パーツ1.D8, R2.Pin_1
  N8: パーツ1.D9, R1.Pin_1
  N9: パーツ1.D10, Disp1.pin_13
  N10: パーツ1.D11/MOSI, Disp1.pin_3
  N11: パーツ1.D12/MISO, Disp1.pin_4
  5V: パーツ1.5V, KMX52-1.VDD, KMX52-1.PSD, KMX52-1.TEST, R9.Pin_0
  N12: パーツ1.A7, KMX52-1.OUT_Z
  N13: パーツ1.A6, KMX52-1.OUT_Y
  N14: パーツ1.A5, KMX52-1.OUT_X
  N15: パーツ1.A4, Disp1.pin_16
  N16: パーツ1.A3, Disp1.pin_15
  N17: パーツ1.A2, Disp1.pin_11
  N18: パーツ1.A1, Disp1.pin_6
  N19: パーツ1.A0, Disp1.pin_10
  N20: パーツ1.D13/SCK, R9.Pin_1, S1.Pin_3, S1.Pin_4
  N21: R1.Pin_0, Disp1.pin_5
  N22: R2.Pin_0, Disp1.pin2
  N23: R3.Pin_0, Disp1.pin_7
  N24: R4.Pin_0, Disp1.pin1
  N25: R5.Pin_0, Disp1.pin_12
  N26: R6.Pin_0, Disp1.pin_8
  N27: R7.Pin_0, Disp1.pin_14
  N28: R8.Pin_0, Disp1.pin_9

custom parts:
  KMX52-1050: 加速度センサー
